# Fritzing sketch Master-Slave switch (saved by Fritzing 0.9.6b)

parts:
  Part1 = Arduino Nano (Rev3.0)
  M1 = 1 chan 5v relay module
  J1 = 120V duplex outlet_1
  J2 = 220v plug
  Mod1 = generic-ac-power-supply [package=THT]
  Part2 = ACS712 Current Sensor 5A 20A 30A

nets:
  GND: Part1.GND, M1.pin_2, Mod1.pin3#3, Part2.GND
  N1: Part1.D2, M1.pin_3
  VIN: Part1.VIN, M1.pin_1, Mod1.pin3#2, Part2.VCC
  N2: Part1.A0, M1.pin_5, J2.pin1, Mod1.pin1, Part2.2, Part2.OUT
  N3: M1.pin_4, J1.H2
  N4: J1.H1, Part2.1
  GND_2: J1.G
  N5: J1.N2, J1.N1, J2.pin2, Mod1.pin2

custom parts:
  1 chan 5v relay module: 1 Channel 5V Relay Module Board Shield with Optocoupler Support High and Low Level Trigger for Arduino.
  120V duplex outlet_1: 120V duplex outlet.
  220v plug: Generic 220V AC plug.
  generic-ac-power-supply: Generic ac power supply module. Use as is, or customize the svgs to fit your particular device (as they are all different.) Provides AC input and single DC output. PCB is generic and will need modifications if you intend to do a pcb mount.
  ACS712 Current Sensor 5A 20A 30A: Remix by Michael Kubina http://www.kubina.info Original by: https://forum.fritzing.org/t/current-sensor-5a-acs712/7694 https://forum.fritzing.org/u/ArtHome ArtHome12@gmail.com

// code stored in the sketch: Master-Slave switch.ino
// Define the pin connections
const int currentSensorPin = A0; // Analog pin for current sensor
const int relayPin = 2;          // Digital pin for relay module

bool relayState = false; // Keeps track of relay state
unsigned long lastTurnOffTime = 0; // Variable to store the time of last turn off

void setup() {
  // Initialize the relay pin as an output
  pinMode(relayPin, OUTPUT);
  // Start serial communication at 9600 baud rate
  Serial.begin(9600);
}

void loop() {
  // Read the analog value from the current sensor
  int sensorValue = analogRead(currentSensorPin);
  
  // Convert the analog value to current in Amperes
  // This calculation depends on the sensitivity of your current sensor
  // The ACS712 sensor outputs about 2.5V when there is no current flowing
  // and the sensitivity is 185mV/A for ACS712-20A, so:
  float current = ((sensorValue - 512) / 1024.0) * 5.0 / 0.185; // ACS712-20A
  
  // Print current value for debugging
  Serial.print("Current: ");
  Serial.print(current);
  Serial.println(" A");
  
  // Check if current exceeds 0.2A (200mA)
  if (current > 0.2) {
    // If relay is not already on, turn it on
    if (!relayState) {
      digitalWrite(relayPin, HIGH);
      relayState = true;
    }
    // Reset last turn off time
    lastTurnOffTime = millis();
  } else {
    // Check if enough time has passed since last turn off
    if (millis() - lastTurnOffTime >= 1000) { // Delay of 1 second (1000 milliseconds)
      // Turn off the relay
      digitalWrite(relayPin, LOW);
      relayState = false;
    }
  }
}
